// Logisim project e2309839.circ as structural Verilog: 1 circuit, main circuit main
module main (
  input  S,
  input  O1,
  input  O0,
  input  A1,
  input  A0,
  input  B1,
  input  B0,
  output E,
  output B,
  output N,
  output L,
  output G,
  output L0,
  output L1,
  output L2,
  output L3,
  output L4,
  output L5,
  output L6,
  output L7
);

  wire and_1_out, and_2_out, and_3_out, and_4_out, and_5_out, and_6_out, and_7_out, and_8_out, and_9_out,
       and_10_out, and_11_out, and_12_out, and_13_out, and_14_out, and_15_out, and_17_out, and_18_out,
       and_19_out, and_20_out, and_24_out, n2_to_4_decoder_x2_74155_1_p3, n2_to_4_decoder_x2_74155_1_p5,
       n2_to_4_decoder_x2_74155_1_p6, n2_to_4_decoder_x2_74155_1_p7, n2_to_4_decoder_x2_74155_1_p8,
       n2_to_4_decoder_x2_74155_2_p4, n2_to_4_decoder_x2_74155_2_p6, n2_to_4_decoder_x2_74155_2_p7,
       n2_to_4_decoder_x2_74155_2_p8, n2_to_4_decoder_x2_74155_2_p9, n2_to_4_decoder_x2_74155_3_p1,
       n2_to_4_decoder_x2_74155_3_p2, n2_to_4_decoder_x2_74155_3_p6, n2_to_4_decoder_x2_74155_3_p7,
       n3_to_8_decoder_74138_1_p5, n3_to_8_decoder_74138_1_p7, n3_to_8_decoder_74138_1_p8,
       n3_to_8_decoder_74138_1_p9, n3_to_8_decoder_74138_1_p10, n3_to_8_decoder_74138_1_p11,
       n3_to_8_decoder_74138_1_p12, n3_to_8_decoder_74138_1_p13, n3_to_8_decoder_74138_1_p14,
       n3_to_8_decoder_74138_1_p15, n3_to_8_decoder_74138_2_p5, n3_to_8_decoder_74138_2_p7,
       n3_to_8_decoder_74138_2_p8, n3_to_8_decoder_74138_2_p9, n3_to_8_decoder_74138_2_p10,
       n3_to_8_decoder_74138_2_p11, n3_to_8_decoder_74138_2_p12, n3_to_8_decoder_74138_2_p13,
       n3_to_8_decoder_74138_2_p14, n3_to_8_decoder_74138_3_p5, n3_to_8_decoder_74138_3_p7,
       n3_to_8_decoder_74138_3_p8, n3_to_8_decoder_74138_3_p9, n3_to_8_decoder_74138_3_p10,
       n3_to_8_decoder_74138_3_p11, n3_to_8_decoder_74138_3_p12, n3_to_8_decoder_74138_3_p13,
       n3_to_8_decoder_74138_3_p14, nor_1_out, not_1_out, not_5_out, not_6_out, not_8_out, not_9_out,
       not_10_out, not_11_out, not_12_out, not_13_out, not_14_out, not_17_out, not_18_out, not_19_out,
       not_20_out, not_21_out, not_22_out, not_23_out, not_24_out, not_27_out, not_28_out, not_29_out,
       not_30_out, not_31_out, not_32_out, not_33_out, not_34_out, not_35_out, not_36_out, not_37_out,
       not_38_out, not_39_out, not_40_out, not_41_out, not_42_out, not_44_out, not_45_out, not_46_out,
       not_47_out, or_1_out, or_2_out, or_3_out, or_4_out, or_10_out, or_11_out, or_12_out, or_13_out,
       or_14_out, or_15_out, or_17_out, xor_1_out, xor_2_out, xor_3_out, xor_4_out, xor_5_out;

  not not_1 (not_1_out, 1'b1);
  and and_1 (and_1_out, A0, 1'b1);
  // _3_to_8_decoder__74138 #(.Facing("east")) 3_to_8_decoder_74138_1: pin names not known; wires that end beside it: S, O1, O0, 1'b1, n3_to_8_decoder_74138_1_p5, n3_to_8_decoder_74138_1_p5, n3_to_8_decoder_74138_1_p7, n3_to_8_decoder_74138_1_p8, n3_to_8_decoder_74138_1_p9, n3_to_8_decoder_74138_1_p10, n3_to_8_decoder_74138_1_p11, n3_to_8_decoder_74138_1_p12, n3_to_8_decoder_74138_1_p13, n3_to_8_decoder_74138_1_p14, n3_to_8_decoder_74138_1_p15
  not not_2 (n3_to_8_decoder_74138_1_p5, 1'b1);
  // NOT_Gate not_3 has open pins: in=A0, out=open
  // NOT_Gate not_4 has open pins: in=A0, out=open
  not not_5 (not_5_out, B1);
  not not_6 (not_6_out, B0);
  and and_2 (and_2_out, not_5_out, not_6_out);
  xor xor_1 (xor_1_out, A0, B0);
  and and_3 (and_3_out, A0, B0);
  xor xor_2 (xor_2_out, A0, B1);
  and and_4 (and_4_out, A0, B1);
  and and_5 (and_5_out, A0, 1'b1);
  and and_6 (and_6_out, A0, not_1_out);
  and and_7 (and_7_out, not_1_out, A0);
  not not_7 (n3_to_8_decoder_74138_1_p15, n3_to_8_decoder_74138_1_p7);
  not not_8 (not_8_out, n3_to_8_decoder_74138_1_p8);
  not not_9 (not_9_out, n3_to_8_decoder_74138_1_p9);
  not not_10 (not_10_out, n3_to_8_decoder_74138_1_p10);
  not not_11 (not_11_out, n3_to_8_decoder_74138_1_p11);
  not not_12 (not_12_out, n3_to_8_decoder_74138_1_p12);
  not not_13 (not_13_out, n3_to_8_decoder_74138_1_p13);
  not not_14 (not_14_out, n3_to_8_decoder_74138_1_p14);
  // _2_to_4_Decoder__x2___74155 #(.Facing("east")) 2_to_4_decoder_x2_74155_1: pin names not known; wires that end beside it: A0, A0, n2_to_4_decoder_x2_74155_1_p3, 1'b1, n2_to_4_decoder_x2_74155_1_p5, n2_to_4_decoder_x2_74155_1_p6, n2_to_4_decoder_x2_74155_1_p7, n2_to_4_decoder_x2_74155_1_p8
  not not_15 (n2_to_4_decoder_x2_74155_1_p3, 1'b1);
  // _2_to_4_Decoder__x2___74155 #(.Facing("east")) 2_to_4_decoder_x2_74155_2: pin names not known; wires that end beside it: not_5_out, B1, B0, n2_to_4_decoder_x2_74155_2_p4, 1'b1, n2_to_4_decoder_x2_74155_2_p6, n2_to_4_decoder_x2_74155_2_p7, n2_to_4_decoder_x2_74155_2_p8, n2_to_4_decoder_x2_74155_2_p9
  not not_16 (n2_to_4_decoder_x2_74155_2_p4, 1'b1);
  and and_8 (and_8_out, A0, A0);
  and and_9 (and_9_out, A0, not_5_out);
  and and_10 (and_10_out, A0, and_2_out);
  and and_11 (and_11_out, A0, B0);
  xor xor_3 (xor_3_out, and_3_out, xor_2_out);
  and and_12 (and_12_out, and_3_out, xor_2_out);
  xor xor_4 (xor_4_out, and_5_out, and_7_out);
  and and_13 (and_13_out, and_5_out, and_7_out);
  and and_14 (and_14_out, and_8_out, not_6_out);
  or or_1 (or_1_out, and_14_out, and_9_out);
  and and_15 (and_15_out, A0, not_6_out);
  or or_2 (or_2_out, and_12_out, and_4_out);
  xor xor_5 (xor_5_out, and_13_out, and_1_out);
  not not_17 (not_17_out, n2_to_4_decoder_x2_74155_1_p5);
  not not_18 (not_18_out, n2_to_4_decoder_x2_74155_1_p6);
  not not_19 (not_19_out, n2_to_4_decoder_x2_74155_1_p7);
  not not_20 (not_20_out, n2_to_4_decoder_x2_74155_1_p8);
  not not_21 (not_21_out, n2_to_4_decoder_x2_74155_2_p6);
  not not_22 (not_22_out, n2_to_4_decoder_x2_74155_2_p7);
  not not_23 (not_23_out, n2_to_4_decoder_x2_74155_2_p8);
  not not_24 (not_24_out, n2_to_4_decoder_x2_74155_2_p9);
  or or_3 (or_3_out, or_1_out, and_10_out);
  or or_4 (or_4_out, and_15_out, and_11_out);
  // _3_to_8_decoder__74138 #(.Facing("east")) 3_to_8_decoder_74138_2: pin names not known; wires that end beside it: xor_1_out, xor_3_out, or_2_out, not_13_out, n3_to_8_decoder_74138_2_p5, n3_to_8_decoder_74138_2_p5, n3_to_8_decoder_74138_2_p7, n3_to_8_decoder_74138_2_p8, n3_to_8_decoder_74138_2_p9, n3_to_8_decoder_74138_2_p10, n3_to_8_decoder_74138_2_p11, n3_to_8_decoder_74138_2_p12, n3_to_8_decoder_74138_2_p13, n3_to_8_decoder_74138_2_p14
  not not_25 (n3_to_8_decoder_74138_2_p5, 1'b1);
  // _3_to_8_decoder__74138 #(.Facing("east")) 3_to_8_decoder_74138_3: pin names not known; wires that end beside it: and_6_out, xor_4_out, xor_5_out, not_10_out, n3_to_8_decoder_74138_3_p5, n3_to_8_decoder_74138_3_p5, n3_to_8_decoder_74138_3_p7, n3_to_8_decoder_74138_3_p8, n3_to_8_decoder_74138_3_p9, n3_to_8_decoder_74138_3_p10, n3_to_8_decoder_74138_3_p11, n3_to_8_decoder_74138_3_p12, n3_to_8_decoder_74138_3_p13, n3_to_8_decoder_74138_3_p14
  not not_26 (n3_to_8_decoder_74138_3_p5, 1'b1);
  and and_16 (G, or_14_out, or_3_out);
  not not_27 (not_27_out, n3_to_8_decoder_74138_2_p7);
  not not_28 (not_28_out, n3_to_8_decoder_74138_2_p8);
  not not_29 (not_29_out, n3_to_8_decoder_74138_2_p9);
  not not_30 (not_30_out, n3_to_8_decoder_74138_2_p10);
  not not_31 (not_31_out, n3_to_8_decoder_74138_2_p11);
  not not_32 (not_32_out, n3_to_8_decoder_74138_2_p12);
  not not_33 (not_33_out, n3_to_8_decoder_74138_2_p13);
  not not_34 (not_34_out, n3_to_8_decoder_74138_2_p14);
  not not_35 (not_35_out, n3_to_8_decoder_74138_3_p7);
  not not_36 (not_36_out, n3_to_8_decoder_74138_3_p8);
  not not_37 (not_37_out, n3_to_8_decoder_74138_3_p9);
  not not_38 (not_38_out, n3_to_8_decoder_74138_3_p10);
  not not_39 (not_39_out, n3_to_8_decoder_74138_3_p11);
  not not_40 (not_40_out, n3_to_8_decoder_74138_3_p12);
  not not_41 (not_41_out, n3_to_8_decoder_74138_3_p13);
  not not_42 (not_42_out, n3_to_8_decoder_74138_3_p14);
  and and_17 (and_17_out, not_17_out, not_21_out);
  and and_18 (and_18_out, not_18_out, not_22_out);
  and and_19 (and_19_out, not_19_out, not_23_out);
  and and_20 (and_20_out, not_24_out, not_20_out);
  or or_5 (L2, not_29_out, not_37_out);
  or or_6 (L3, not_30_out, not_38_out);
  or or_7 (L4, not_31_out, not_39_out);
  or or_8 (L5, not_40_out, not_32_out);
  or or_9 (L7, not_34_out, not_42_out);
  or or_10 (or_10_out, and_17_out, and_18_out);
  or or_11 (or_11_out, or_10_out, or_12_out);
  or or_12 (or_12_out, and_19_out, and_20_out);
  or or_13 (or_13_out, not_28_out, not_36_out);
  or or_14 (or_14_out, n3_to_8_decoder_74138_1_p15, not_8_out);
  or or_15 (or_15_out, not_11_out, not_12_out);
  or or_16 (L6, not_33_out, not_41_out);
  // _2_to_4_Decoder__x2___74155 #(.Facing("east")) 2_to_4_decoder_x2_74155_3: pin names not known; wires that end beside it: n2_to_4_decoder_x2_74155_3_p1, n2_to_4_decoder_x2_74155_3_p2, not_9_out, n2_to_4_decoder_x2_74155_3_p2, n2_to_4_decoder_x2_74155_3_p2, n2_to_4_decoder_x2_74155_3_p6, n2_to_4_decoder_x2_74155_3_p7
  and and_21 (n2_to_4_decoder_x2_74155_3_p1, not_9_out, A0);
  and and_22 (E, or_14_out, or_11_out);
  or or_17 (or_17_out, not_27_out, not_35_out);
  not not_43 (n2_to_4_decoder_x2_74155_3_p2, 1'b1);
  and and_23 (B, or_15_out, or_4_out);
  not not_44 (not_44_out, or_11_out);
  not not_45 (not_45_out, or_3_out);
  nor nor_1 (nor_1_out, E, G);
  or or_18 (L0, or_17_out, not_46_out);
  not not_46 (not_46_out, n2_to_4_decoder_x2_74155_3_p6);
  not not_47 (not_47_out, n2_to_4_decoder_x2_74155_3_p7);
  and and_24 (and_24_out, not_44_out, not_45_out);
  and and_25 (L, or_14_out, nor_1_out);
  or or_19 (L1, or_13_out, not_47_out);
  and and_26 (N, and_24_out, not_14_out);

  assign A1 = A0;
endmodule
